// Logisim project xor.circ as structural Verilog: 1 circuit, main circuit main
module main (
);

  wire and_1_out, and_2_out, clock_1_out, not_1_out, not_2_out, or_1_out;

  Clock clock_1 (.out(clock_1_out));
  not not_1 (not_1_out, clock_1_out);
  not not_2 (not_2_out, 1'b1);
  and and_1 (and_1_out, 1'b1, not_1_out);
  and and_2 (and_2_out, not_2_out, clock_1_out);
  or or_1 (or_1_out, and_1_out, and_2_out);
endmodule
